# Fritzing sketch Schematic (saved by Fritzing 0.8.7b)
breadboards: 1

parts:
  Part1 = Adafruit DS3231 [part_number="Adafruit #3013"]
  OLED_I2C1 = OLED 128x64 I2C Monochrome Display
  Part2 = Arduino Nano (Rev3.0)

nets:
  VIN: Part1.Vin, OLED_I2C1.VDD, Part2.5V
  GND: Part1.GND, OLED_I2C1.GND, Part2.GND
  N1: Part1.SCL, OLED_I2C1.SCK, Part2.A5
  N2: Part1.SDA, OLED_I2C1.SDA, Part2.A4

custom parts:
  Adafruit DS3231: The datasheet for the DS3231 explains that this part is an "Extremely Accurate I²C-Integrated RTC/TCXO/Crystal". And, hey, it does exactly what it says on the tin! This Real Time Clock (RTC) is the most precise you can get in a small, low power package. Most RTCs use an external 32kHz timing crystal that is used to keep time with low current draw. And that's all well and good, but those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
